# Fritzing sketch motor_board (saved by Fritzing 0.9.3b)
breadboards: 1

parts:
  Часть1 = Arduino Uno (Rev3) - ICSP
  IC1 = L293D [package=THT]  # not connected
  M1 = Stepper Motor - Bipolar  # not connected
  VCC1 = Battery block 9V

nets:
  N1: Часть1.GND, VCC1.-
